# Fritzing sketch lightning-trigger (saved by Fritzing 0.9.3b)
breadboards: 1

parts:
  Bauteil1 = Arduino Uno (Rev3)
  LED1 = LED - 5mm [color="Red (633nm)" package="5 mm [THT]"]
  R1 = Resistor [tolerance=±5% resistance=220 package=THT]
  R2 = Photocell (LDR) [package=THT]
  R3 = Resistor [tolerance=±5% resistance=1k package=THT]

nets:
  N1: Bauteil1.A0, R2.pin_0, R3.Pin_1
  N2: Bauteil1.GND, LED1.cathode, R3.Pin_0
  N3: Bauteil1.D5_PWM, R1.Pin_1
  N4: Bauteil1.5V, R2.pin_1
  N5: LED1.anode, R1.Pin_0
